// Digital circuit BabylonianClock.dig as structural Verilog
module BabylonianClock (
  input  CLK,
  input  CLR,
  input  SETUP,
  input  MIN_ADV,
  input  HOUR_ADV,
  output [5:0] SECONDS,
  output [5:0] MINUTES,
  output [4:0] HOURS
);

  wire and_1_out, and_2_out, and_3_out, and_4_out, and_5_out, and_6_out, and_7_out, and_8_out, d_ff_1_q,
       d_ff_2_q, or_1_out, or_2_out, or_3_out, or_4_out, or_5_out, xor_1_out, xor_2_out, xor_3_out;

  and and_1 (and_1_out, ~SETUP, CLK);  // And
  xor xor_1 (xor_1_out, and_1_out, CLR);
  or or_1 (or_1_out, CLR, and_3_out);
  D_FF d_ff_1 (.D(and_3_out), .C(CLK), .Q(d_ff_1_q));  // open: nQ
  CounterPreset #(.Bits(6)) counterpreset_1 (
    .en(1'b1), .C(xor_1_out), .dir(1'b0), .in(6'b000001), .ld(1'b0), .clr(or_1_out), .out(SECONDS));  // open: ovf
  and and_2 (and_2_out, ~SETUP, d_ff_1_q);  // And
  and and_3 (and_3_out, SECONDS[5], SECONDS[4], SECONDS[3], SECONDS[1], SECONDS[0]);
  and and_4 (and_4_out, MIN_ADV, SETUP);
  or or_2 (or_2_out, and_4_out, and_2_out);
  xor xor_2 (xor_2_out, or_2_out, CLR);
  or or_3 (or_3_out, CLR, and_6_out);
  D_FF d_ff_2 (.D(and_6_out), .C(xor_2_out), .Q(d_ff_2_q));  // open: nQ
  CounterPreset #(.Bits(6)) counterpreset_2 (
    .en(1'b1), .C(xor_2_out), .dir(1'b0), .in(6'b000001), .ld(1'b0), .clr(or_3_out), .out(MINUTES));  // open: ovf
  and and_5 (and_5_out, ~SETUP, d_ff_2_q);  // And
  and and_6 (and_6_out, MINUTES[5], MINUTES[4], MINUTES[3], MINUTES[1], MINUTES[0]);
  or or_4 (or_4_out, and_7_out, and_5_out);
  and and_7 (and_7_out, HOUR_ADV, SETUP);
  xor xor_3 (xor_3_out, or_4_out, CLR);
  or or_5 (or_5_out, CLR, and_8_out);
  CounterPreset #(.Bits(5)) counterpreset_3 (
    .en(1'b1), .C(xor_3_out), .dir(1'b0), .in(5'b00001), .ld(1'b0), .clr(or_5_out), .out(HOURS));  // open: ovf
  and and_8 (and_8_out, HOURS[4], HOURS[2], HOURS[1], HOURS[0]);

  // Notes on the sheet:
  //   CLK: Hz: 120
endmodule
