// Digital circuit LeapCalculator.dig as structural Verilog
module LeapCalculator (
  input  [10:0] IN,
  output IS_LEAP
);

  wire [21:0] add_1_s, div_1_r, mul_1_mul;

  Mul #(.Bits(11)) mul_1 (.a(11'h34), .b(IN), .mul(mul_1_mul));
  Add #(.Bits(22)) add_1 (.a(22'h92), .b(mul_1_mul), .c_i(1'b0), .s(add_1_s));  // open: c_o
  Div #(.Bits(22)) div_1 (.a(add_1_s), .b(22'h125), .r(div_1_r));  // open: q
  Comparator #(.Bits(22)) comparator_1 (.a(div_1_r), .b(22'h34), .lt(IS_LEAP));  // open: gt, eq
  // Probe on div_1_r
endmodule
