// Digital circuit RobertsonMultiplier.dig as structural Verilog
module RobertsonMultiplier (
  input  CLK,
  input  MULTIPLY,
  input  [15:0] MULTIPLIER,
  input  [15:0] MULTIPLICAND,
  output [31:0] PRODUCT,
  output END
);

  wire and_2_out, BEGIN, controlunit_1_ex_op, multiplexer_1_out, xor_1_out;
  wire [1:0] and_1_out;
  wire [4:0] counter_1_out;
  wire [15:0] _16bitaddersubtractor_1_result, d_ff_as_1_q;

  _16BitShifter u_Multiplier (
    .CLK(CLK), .CLR(MULTIPLY), .LOAD(BEGIN), .SHIFT(and_1_out[1]), .DATA_IN(MULTIPLIER),
    .SHIFT_IN(PRODUCT[16]), .DATA_OUT(PRODUCT[15:0]));
  _16BitShifter Accamulator (
    .CLK(CLK), .CLR(MULTIPLY), .LOAD(and_1_out[0]), .SHIFT(and_1_out[1]),
    .DATA_IN(_16bitaddersubtractor_1_result), .SHIFT_IN(multiplexer_1_out), .DATA_OUT(PRODUCT[31:16]));
  ControlUnit controlunit_1 (
    .CLK(CLK), .BEGIN(MULTIPLY), .END(END), .INIT(BEGIN), .EX_OP(controlunit_1_ex_op), .SHIFT(and_1_out[1]));
  and and_1 (and_1_out[0], PRODUCT[0], controlunit_1_ex_op);
  Multiplexer multiplexer_1 (
    .sel(counter_1_out[4]), .in_0(d_ff_as_1_q[15]), .in_1(PRODUCT[31]), .out(multiplexer_1_out));
  // Probe on PRODUCT
  xor xor_1 (xor_1_out, controlunit_1_ex_op, BEGIN);
  D_FF_AS #(.Bits(16)) d_ff_as_1 (
    .Set(1'b0), .D(MULTIPLICAND), .C(and_2_out), .Clr(BEGIN), .Q(d_ff_as_1_q));  // open: nQ
  Counter #(.Bits(5)) counter_1 (.en(1'b1), .C(xor_1_out), .clr(BEGIN), .out(counter_1_out));  // open: ovf
  and and_2 (and_2_out, CLK, PRODUCT[0]);
  _16BitAdderSubtractor _16bitaddersubtractor_1 (
    .A(PRODUCT[31:16]), .B(MULTIPLICAND), .AS(counter_1_out[4]), .RESULT(_16bitaddersubtractor_1_result));  // open: C_OUT

  // Other names for the same wires on the sheet: CLK_T = CLK; MLD[15:0] = MULTIPLICAND; MLT[15:0] = MULTIPLIER

  // Notes on the sheet:
  //   CLK: Hz: 200
endmodule
