// Digital circuit RobertsonMultiplierMoore.dig as structural Verilog
module RobertsonMultiplierMoore (
  input  CLK,
  input  MULTIPLY,
  input  [15:0] MULTIPLIER,
  input  [15:0] MULTIPLICAND,
  output [31:0] PRODUCT,
  output END
);

  wire and_2_out, and_3_out, and_4_out, COMP_T, delay_1_out, EX_OP, INIT, multiplexer_1_out, SHIFT, xor_1_out;
  wire [0:0] and_1_out;
  wire [3:0] counter_1_out;
  wire [15:0] _16bitaddersubtractor_1_result, d_ff_as_1_q;

  _16BitShifter u_Multiplier (
    .CLK(CLK), .CLR(1'b0), .LOAD(INIT), .SHIFT(SHIFT), .DATA_IN(MULTIPLIER), .SHIFT_IN(PRODUCT[16]),
    .DATA_OUT(PRODUCT[15:0]));
  _16BitShifter Accamulator (
    .CLK(CLK), .CLR(MULTIPLY), .LOAD(and_1_out[0]), .SHIFT(SHIFT), .DATA_IN(_16bitaddersubtractor_1_result),
    .SHIFT_IN(multiplexer_1_out), .DATA_OUT(PRODUCT[31:16]));
  Delay #(.delayTime(16)) delay_1 (.in(CLK), .out(delay_1_out));
  and and_1 (and_1_out[0], PRODUCT[0], EX_OP);
  Multiplexer multiplexer_1 (.sel(COMP_T), .in_0(d_ff_as_1_q[15]), .in_1(PRODUCT[31]), .out(multiplexer_1_out));
  // Probe on PRODUCT
  and and_2 (and_2_out, delay_1_out, SHIFT);
  xor xor_1 (xor_1_out, and_2_out, INIT);
  Counter #(.Bits(5)) counter_1 (.en(1'b1), .C(xor_1_out), .clr(INIT), .out({COMP_T, counter_1_out}));  // open: ovf
  D_FF_AS #(.Bits(16)) d_ff_as_1 (
    .Set(1'b0), .D(MULTIPLICAND), .C(and_4_out), .Clr(INIT), .Q(d_ff_as_1_q));  // open: nQ
  and and_3 (and_3_out, counter_1_out[0], counter_1_out[1], counter_1_out[2], counter_1_out[3]);
  and and_4 (and_4_out, CLK, PRODUCT[0]);
  _16BitAdderSubtractor _16bitaddersubtractor_1 (
    .A(PRODUCT[31:16]), .B(MULTIPLICAND), .AS(and_3_out), .RESULT(_16bitaddersubtractor_1_result));  // open: C_OUT

  // Other names for the same wires on the sheet: _2LSB = PRODUCT[1]; BEGIN = MULTIPLY; CLK_T = CLK; END_T = END;
  //   MLD[15:0] = MULTIPLICAND; MLT[15:0] = MULTIPLIER

  // Notes on the sheet:
  //   CLK: Hz: 8
  //   Your More FSM
endmodule

/* Test case Test Vectors:
            CLK MULTIPLY MULTIPLIER MULTIPLICAND PRODUCT
            C   0        0          0            0

# 0x0000 x 0x0000 = 0x00000000

            C   1        0x0000     0x0000       X
repeat(33)  C   0        0x0000     0x0000       X
	    C   0        0x0000     0x0000       0x00000000

# 0x0001 x 0x0001 = 0x00000001

            C   1        0x0001     0x0001       X
repeat(33)  C   0        0x0001     0x0001       X
	    C   0        0x0001     0x0001       0x00000001

# 0x0001 x 0x5555 = 0x00005555

            C   1        0x0001     0x5555       X
repeat(33)  C   0        0x0001     0x5555       X
	    C   0        0x0001     0x5555       0x00005555

# 0x5555 x 0x5555 = 0x1C718E39

            C   1        0x5555     0x5555       X
repeat(33)  C   0        0x5555     0x5555       X
	    C   0        0x5555     0x5555       0x1C718E39

# 0xFFFF x 0x5555 = 0xFFFFAAAB

            C   1        0xFFFF     0x5555       X
repeat(33)  C   0        0xFFFF     0x5555       X
	    C   0        0xFFFF     0x5555       0xFFFFAAAB

# 0xFFFF x 0xFFFF = 0x00000001

            C   1        0xFFFF     0xFFFF       X
repeat(33)  C   0        0xFFFF     0xFFFF       X
	    C   0        0xFFFF     0xFFFF       0x00000001

# 0xAAAA x 0xFFFF = 0x00005556

            C   1        0xAAAA     0xFFFF       X
repeat(33)  C   0        0xAAAA     0xFFFF       X
	    C   0        0xAAAA     0xFFFF       0x00005556

# 0x0000 x 0xAAAA = 0x00000000

            C   1        0x0000     0xAAAA       X
repeat(33)  C   0        0x0000     0xAAAA       X
	    C   0        0x0000     0xAAAA       0x00000000

# 0xFFFF x 0xAAAA = 0x00005556

            C   1        0xFFFF     0xAAAA       X
repeat(33)  C   0        0xFFFF     0xAAAA       X
	    C   0        0xFFFF     0xAAAA       0x00005556

# 0xAAAA x 0xAAAA = 0x1C7238E4

            C   1        0xAAAA     0xAAAA       X
repeat(33)  C   0        0xAAAA     0xAAAA       X
	    C   0        0xAAAA     0xAAAA       0x1C7238E4

# 0x8000 x 0xFFFF = 0x00008000

            C   1        0x8000     0xFFFF       X
repeat(33)  C   0        0x8000     0xFFFF       X
	    C   0        0x8000     0xFFFF       0x00008000

# 0xFAFA x 0x000 = 0x00000000

            C   1        0xFAFA     0x0000       X
repeat(33)  C   0        0xFAFA     0x0000       X
	    C   0        0xFAFA     0x0000       0x00000000

# 0x0001 x 0xFFFF = 0xFFFFFFFF

            C   1        0x0001     0xFFFF       X
repeat(33)  C   0        0x0001     0xFFFF       X
	    C   0        0x0001     0xFFFF       0xFFFFFFFF

# 0xFFFF x 0x0001 = 0xFFFFFFFF

            C   1        0xFFFF     0x0001       X
repeat(33)  C   0        0xFFFF     0x0001       X
	    C   0        0xFFFF     0x0001       0xFFFFFFFF

# 0x3333 x 0xCCCC = 0xF5C270A4

            C   1        0x3333     0xCCCC       X
repeat(33)  C   0        0x3333     0xCCCC       X
	    C   0        0x3333     0xCCCC       0xF5C270A4
*/
