// Digital circuit BabylonianAlarm.dig as structural Verilog
module BabylonianAlarm (
  input  CLR,
  input  SETUP,
  input  MIN_ADV,
  input  HOUR_ADV,
  output [5:0] MINUTES,
  output [4:0] HOURS
);

  wire and_1_out, and_2_out, and_3_out, and_4_out, or_1_out, or_2_out, xor_1_out, xor_2_out;

  and and_1 (and_1_out, MIN_ADV, SETUP);
  xor xor_1 (xor_1_out, and_1_out, CLR);
  or or_1 (or_1_out, CLR, and_2_out);
  CounterPreset #(.Bits(6)) counterpreset_1 (
    .en(1'b1), .C(xor_1_out), .dir(1'b0), .in(6'b000001), .ld(1'b0), .clr(or_1_out), .out(MINUTES));  // open: ovf
  and and_2 (and_2_out, MINUTES[5], MINUTES[4], MINUTES[3], MINUTES[1], MINUTES[0]);
  and and_3 (and_3_out, HOUR_ADV, SETUP);
  xor xor_2 (xor_2_out, and_3_out, CLR);
  or or_2 (or_2_out, CLR, and_4_out);
  CounterPreset #(.Bits(5)) counterpreset_2 (
    .en(1'b1), .C(xor_2_out), .dir(1'b0), .in(5'b00001), .ld(1'b0), .clr(or_2_out), .out(HOURS));  // open: ovf
  and and_4 (and_4_out, HOURS[4], HOURS[2], HOURS[1], HOURS[0]);
endmodule
