// Digital circuit 16BitAdderSubtractor.dig as structural Verilog
module _16BitAdderSubtractor (
  input  [15:0] A,
  input  [15:0] B,
  input  AS,
  output [15:0] RESULT,
  output C_OUT
);

  wire [15:0] multiplexer_1_out, neg_1_out;

  Neg #(.Bits(16)) neg_1 (.in(B), .out(neg_1_out));
  Multiplexer #(.Bits(16)) multiplexer_1 (.sel(AS), .in_0(B), .in_1(neg_1_out), .out(multiplexer_1_out));
  // Probe on neg_1_out
  Add #(.Bits(16)) add_1 (.a(A), .b(multiplexer_1_out), .c_i(1'b0), .s(RESULT), .c_o(C_OUT));
endmodule
