// Digital circuit 17BitAdderSubtractor.dig as structural Verilog
module _17BitAdderSubtractor (
  input  [16:0] A,
  input  [16:0] B,
  input  AS,
  output [16:0] RESULT,
  output C_OUT
);

  wire [16:0] multiplexer_1_out, neg_1_out;

  Neg #(.Bits(17)) neg_1 (.in(B), .out(neg_1_out));
  Multiplexer #(.Bits(17)) multiplexer_1 (.sel(AS), .in_0(B), .in_1(neg_1_out), .out(multiplexer_1_out));
  // Probe on neg_1_out
  Add #(.Bits(17)) add_1 (.a(A), .b(multiplexer_1_out), .c_i(1'b0), .s(RESULT), .c_o(C_OUT));
endmodule
