// Digital circuit 17BitShifter.dig as structural Verilog
module _17BitShifter (
  input  CLK,
  input  CLR,
  input  LOAD,
  input  SHIFT,
  input  [16:0] DATA_IN,
  input  SHIFT_IN,
  output [16:0] DATA_OUT
);

  ShiftBit shiftbit_1 (
    .EN(SHIFT), .SHIFT_IN(SHIFT_IN), .LOAD(LOAD), .BIT_IN(DATA_IN[16]), .CLR(CLR), .CLK(CLK),
    .OUT(DATA_OUT[16]));
  ShiftBit shiftbit_2 (
    .EN(SHIFT), .SHIFT_IN(DATA_OUT[16]), .LOAD(LOAD), .BIT_IN(DATA_IN[15]), .CLR(CLR), .CLK(CLK),
    .OUT(DATA_OUT[15]));
  ShiftBit shiftbit_3 (
    .EN(SHIFT), .SHIFT_IN(DATA_OUT[15]), .LOAD(LOAD), .BIT_IN(DATA_IN[14]), .CLR(CLR), .CLK(CLK),
    .OUT(DATA_OUT[14]));
  ShiftBit shiftbit_4 (
    .EN(SHIFT), .SHIFT_IN(DATA_OUT[14]), .LOAD(LOAD), .BIT_IN(DATA_IN[13]), .CLR(CLR), .CLK(CLK),
    .OUT(DATA_OUT[13]));
  ShiftBit shiftbit_5 (
    .EN(SHIFT), .SHIFT_IN(DATA_OUT[13]), .LOAD(LOAD), .BIT_IN(DATA_IN[12]), .CLR(CLR), .CLK(CLK),
    .OUT(DATA_OUT[12]));
  ShiftBit shiftbit_6 (
    .EN(SHIFT), .SHIFT_IN(DATA_OUT[12]), .LOAD(LOAD), .BIT_IN(DATA_IN[11]), .CLR(CLR), .CLK(CLK),
    .OUT(DATA_OUT[11]));
  ShiftBit shiftbit_7 (
    .EN(SHIFT), .SHIFT_IN(DATA_OUT[11]), .LOAD(LOAD), .BIT_IN(DATA_IN[10]), .CLR(CLR), .CLK(CLK),
    .OUT(DATA_OUT[10]));
  ShiftBit shiftbit_8 (
    .EN(SHIFT), .SHIFT_IN(DATA_OUT[10]), .LOAD(LOAD), .BIT_IN(DATA_IN[9]), .CLR(CLR), .CLK(CLK),
    .OUT(DATA_OUT[9]));
  ShiftBit shiftbit_9 (
    .EN(SHIFT), .SHIFT_IN(DATA_OUT[9]), .LOAD(LOAD), .BIT_IN(DATA_IN[8]), .CLR(CLR), .CLK(CLK),
    .OUT(DATA_OUT[8]));
  ShiftBit shiftbit_10 (
    .EN(SHIFT), .SHIFT_IN(DATA_OUT[8]), .LOAD(LOAD), .BIT_IN(DATA_IN[7]), .CLR(CLR), .CLK(CLK),
    .OUT(DATA_OUT[7]));
  ShiftBit shiftbit_11 (
    .EN(SHIFT), .SHIFT_IN(DATA_OUT[7]), .LOAD(LOAD), .BIT_IN(DATA_IN[6]), .CLR(CLR), .CLK(CLK),
    .OUT(DATA_OUT[6]));
  ShiftBit shiftbit_12 (
    .EN(SHIFT), .SHIFT_IN(DATA_OUT[6]), .LOAD(LOAD), .BIT_IN(DATA_IN[5]), .CLR(CLR), .CLK(CLK),
    .OUT(DATA_OUT[5]));
  ShiftBit shiftbit_13 (
    .EN(SHIFT), .SHIFT_IN(DATA_OUT[5]), .LOAD(LOAD), .BIT_IN(DATA_IN[4]), .CLR(CLR), .CLK(CLK),
    .OUT(DATA_OUT[4]));
  ShiftBit shiftbit_14 (
    .EN(SHIFT), .SHIFT_IN(DATA_OUT[4]), .LOAD(LOAD), .BIT_IN(DATA_IN[3]), .CLR(CLR), .CLK(CLK),
    .OUT(DATA_OUT[3]));
  ShiftBit shiftbit_15 (
    .EN(SHIFT), .SHIFT_IN(DATA_OUT[3]), .LOAD(LOAD), .BIT_IN(DATA_IN[2]), .CLR(CLR), .CLK(CLK),
    .OUT(DATA_OUT[2]));
  ShiftBit shiftbit_16 (
    .EN(SHIFT), .SHIFT_IN(DATA_OUT[2]), .LOAD(LOAD), .BIT_IN(DATA_IN[1]), .CLR(CLR), .CLK(CLK),
    .OUT(DATA_OUT[1]));
  ShiftBit shiftbit_17 (
    .EN(SHIFT), .SHIFT_IN(DATA_OUT[1]), .LOAD(LOAD), .BIT_IN(DATA_IN[0]), .CLR(CLR), .CLK(CLK),
    .OUT(DATA_OUT[0]));
endmodule
