// Digital circuit ShiftBit.dig as structural Verilog
module ShiftBit (
  input  EN,
  input  SHIFT_IN,
  input  LOAD,
  input  BIT_IN,
  input  CLR,
  input  CLK,
  output OUT
);

  wire and_1_out, and_2_out, multiplexer_1_out, or_1_out, or_2_out;

  and and_1 (and_1_out, EN, SHIFT_IN);
  and and_2 (and_2_out, LOAD, BIT_IN);
  or or_1 (or_1_out, and_1_out, and_2_out);
  or or_2 (or_2_out, LOAD, EN);
  Multiplexer multiplexer_1 (.sel(or_2_out), .in_0(OUT), .in_1(or_1_out), .out(multiplexer_1_out));
  D_FF_AS d_ff_as_1 (.Set(1'b0), .D(multiplexer_1_out), .C(CLK), .Clr(CLR), .Q(OUT));  // open: nQ
endmodule
