// Digital circuit AndD.dig as structural Verilog
module AndD (
  output Q
);

  wire and_1_out, undriven, undriven_2, undriven_3, undriven_4;

  and and_1 (and_1_out, undriven, undriven_2, undriven_3, undriven_4, 1'b1, 1'b1, 1'b1, 1'b1, 1'b1);
  Delay #(.generic("initD := 2; riseD := 1; this.delayTime = initD + (riseD * args.inputCount);")) delay_1 (
    .in(and_1_out), .out(Q));
endmodule

/* Code that sets the parameters or builds the circuit:
inputCount := 1;
*/

/* Code that sets the parameters or builds the circuit:
for (i:=0; i <args.inputCount; i++) {
 inp:=addComponent("In",0,i);
 inp.Label="D" + i;
}
*/
