// Digital circuit Corrector.dig as structural Verilog
module Corrector (
  input  [3:0] SUM,
  input  SEL,
  output [3:0] OUT
);

  wire and_1_out, not_1_out, not_2_out, not_3_out, not_5_out, not_6_out, not_7_out, or_1_out, or_2_out,
       or_3_out, or_4_out, or_5_out, xor_1_out, xor_2_out, xor_3_out;
  wire [3:1] not_4_out;

  xor xor_1 (xor_1_out, SUM[2], SEL);
  or or_1 (or_1_out, xor_2_out, xor_1_out);
  xor xor_2 (xor_2_out, SUM[1], SEL);
  not not_1 (not_1_out, SUM[3]);
  or or_2 (or_2_out, SUM[2], SUM[3]);
  xor xor_3 (xor_3_out, SUM[1], SEL);
  xor xor_4 (not_4_out[3], SUM[3], or_1_out);
  not not_2 (not_2_out, SUM[2]);
  or or_3 (or_3_out, not_2_out, not_1_out);
  not not_3 (not_3_out, SUM[2]);
  not not_4 (not_4_out[1], SUM[1]);
  xor xor_5 (not_4_out[2], not_3_out, xor_3_out);
  not not_5 (not_5_out, SUM[1]);
  not not_6 (not_6_out, SUM[3]);
  or or_4 (or_4_out, SUM[0], SUM[1], SUM[3]);
  not not_7 (not_7_out, SUM[0]);
  or or_5 (or_5_out, not_7_out, not_5_out, not_6_out);
  and and_1 (and_1_out, or_5_out, or_4_out, or_3_out, or_2_out);
  Multiplexer #(.Bits(4)) multiplexer_1 (.sel(and_1_out), .in_0(SUM), .in_1({not_4_out, SUM[0]}), .out(OUT));
endmodule
