// Digital circuit NorD.dig as structural Verilog
module NorD (
  output Q
);

  wire nor_1_out, undriven, undriven_2, undriven_3, undriven_4;

  nor nor_1 (nor_1_out, undriven, undriven_2, undriven_3, undriven_4, 1'b0, 1'b0, 1'b0, 1'b0, 1'b0);
  Delay #(.generic("initD := 0; riseD := 1; this.delayTime = initD + (riseD * args.inputCount);")) delay_1 (
    .in(nor_1_out), .out(Q));
endmodule

/* Code that sets the parameters or builds the circuit:
inputCount := 6;
*/

/* Code that sets the parameters or builds the circuit:
for (i:=0; i <args.inputCount; i++) {
 inp:=addComponent("In",0,i);
 inp.Label="D" + i;
}
*/
