// Digital circuit SimpleSuperController.dig as structural Verilog
module SimpleSuperController (
  input  BEGIN,
  input  CLK,
  input  PHASE_END,
  output [1:0] PHASE,
  output BEGIN_PHASE
);

  wire and_1_out, d_ff_1_q, or_1_out, xor_1_out;

  xor xor_1 (xor_1_out, PHASE_END, BEGIN);
  or or_1 (or_1_out, BEGIN, PHASE_END);
  CounterPreset #(.Bits(2)) counterpreset_1 (
    .en(1'b1), .C(xor_1_out), .dir(1'b0), .in(2'b01), .ld(BEGIN), .clr(1'b0), .out(PHASE));  // open: ovf
  D_FF d_ff_1 (.D(or_1_out), .C(CLK), .Q(d_ff_1_q));  // open: nQ
  and and_1 (and_1_out, PHASE[0], PHASE[1]);
  and and_2 (BEGIN_PHASE, ~and_1_out, d_ff_1_q);  // And

  // Notes on the sheet:
  //   CLK: Hz: 5
endmodule
