// Digital circuit PotatoCounter.dig as structural Verilog
module PotatoCounter (
  input  [1:0] IN,
  input  CLK,
  input  RST,
  output EMPTY,
  output [3:0] Count
);

  wire and_1_out, and_2_out;
  wire [3:0] add_1_s, d_ff_as_1_q, multiplexer_1_out, multiplexer_2_out;

  and and_1 (and_1_out, ~EMPTY, CLK);  // And
  D_FF_AS #(.Bits(4)) d_ff_as_1 (
    .Set(1'b0), .D(multiplexer_2_out), .C(and_1_out), .Clr(RST), .Q(d_ff_as_1_q));  // open: nQ
  Multiplexer #(.Bits(4)) multiplexer_1 (.sel(and_2_out), .in_0(4'b0001), .in_1(4'b0010), .out(multiplexer_1_out));
  and and_2 (and_2_out, IN[0], IN[1]);
  Add #(.Bits(4)) add_1 (.a(d_ff_as_1_q), .b(multiplexer_1_out), .c_i(1'b0), .s(add_1_s));  // open: c_o
  Multiplexer #(.Bits(4)) multiplexer_2 (.sel(IN[1]), .in_0(d_ff_as_1_q), .in_1(add_1_s), .out(multiplexer_2_out));
  Sub #(.Bits(4)) sub_1 (.a(4'b1111), .b(d_ff_as_1_q), .c_i(1'b0), .s(Count));  // open: c_o
  nor nor_1 (EMPTY, Count[0], Count[1], Count[2], Count[3]);
endmodule
